# Fritzing sketch And gate (saved by Fritzing 0.8.7b)
breadboards: 1

parts:
  Part1 = Arduino Uno (Rev3)
  Grove1 = Grove Button [part_number="LED BUTTON"]
  Grove2 = Grove Button [part_number="LED BUTTON"]
  Grove3 = Grove Button [part_number=RESET]
  Printer = Thermal Printer

nets:
  N1: Part1.A1, Grove3.NC
  N2: Part1.D8, Grove2.NC
  N3: Part1.D2, Grove1.NC
  N4: Part1.D3_PWM, Grove1.SIG
  N5: Part1.D5_PWM, Printer.TXD
  N6: Part1.D6_PWM, Printer.RXD
  N7: Part1.D7, Grove2.SIG
  VCC: Part1.5V, Grove1.VCC, Grove2.VCC, Grove3.VCC
  GND: Grove1.GND, Grove2.GND, Grove3.GND, Printer.GND#2
  5V: Printer.VH

notes:
  NC
  1.5 A
